# Fritzing sketch waterbot (saved by Fritzing 0.9.3b)
breadboards: 1

parts:
  Part1 = Arduino Nano (Rev3.0)
  Q1 = TRANSISTOR_NPN [package=to-92-ammo]
  M1 = DC Motor
  J1 = Basic Servo
  Adafruit_HUZZAH_ESP8266_Breakout1 = Adafruit HUZZAH ESP8266 Breakout [part_number=2471]  # not connected

nets:
  N1: Part1.GND, M1.pin_1
  N2: Part1.D2, Q1.B
  N3: Part1.D3, J1.pulse
  5V: Part1.5V, Q1.C, J1.vcc
  N4: Q1.E, M1.pin_2
